# Fritzing sketch two_color_led (saved by Fritzing 0.9.2b)
breadboards: 1

parts:
  Part1 = Arduino Nano (Rev3.0)
  LED1 = DUO LED RG [package="5 mm [THT]"]
  R1 = Resistor [tolerance=±5% resistance=330 package="2010 [SMD]"]
  R2 = Resistor [tolerance=±5% resistance=330 package="2010 [SMD]"]

nets:
  N1: Part1.GND, LED1.green_anode
  N2: Part1.D10, R2.Pin_0
  N3: Part1.D11/MOSI, R1.Pin_0
  N4: LED1.red_anode, R1.Pin_1
  N5: LED1.common_cathode, R2.Pin_1
